// Logisim project CPU_LAB4.circ as structural Verilog: 3 circuits, main circuit main
module main (
  input  [3:0] in_1,
  input  [3:0] in_2,
  input  [3:0] in_3,
  input  [3:0] in_4,
  input  Clk,
  output [7:0] PC_out,
  output [4:0] Instruction_Address_Out,
  output [3:0] Reg0_Out,
  output [3:0] Reg1_Out,
  output [3:0] Reg2_Out,
  output [3:0] Reg3_Out,
  output [3:0] Reg4_Out,
  output [3:0] Reg5_Out,
  output [3:0] Reg6_Out,
  output [3:0] Reg7_Out,
  output [3:0] Reg8_Out,
  output [3:0] Reg9_Out,
  output [3:0] Reg10_Out,
  output [3:0] Reg11_Out,
  output [3:0] Reg12_Out,
  output [3:0] Reg13_Out,
  output [3:0] Reg14_Out,
  output [3:0] Reg15_Out
);

  wire and_1_out, and_2_out, and_3_out, I_Type, not_1_out, not_2_out, not_3_out, not_4_out, not_5_out,
       RegWrite;
  wire [3:0] A_Value, B_Sel, B_Value, Data, Imm;

  Demultiplexer #(.width(4), .enable("false")) demultiplexer_1 (.out0(B_Sel), .out1(Imm), .in(in_3), .sel(I_Type));
  not not_1 (not_1_out, in_1[0]);
  and and_1 (and_1_out, not_1_out, in_1[2]);
  not not_2 (not_2_out, in_1[2]);
  and and_2 (and_2_out, in_1[0], in_1[1], not_2_out, not_3_out);
  not not_3 (not_3_out, in_1[3]);
  not not_4 (not_4_out, in_1[0]);
  and and_3 (and_3_out, not_4_out, in_1[3], not_5_out);
  not not_5 (not_5_out, in_1[1]);
  or or_1 (RegWrite, in_1[1], in_1[2], in_1[3]);
  or or_2 (I_Type, and_1_out, and_2_out, and_3_out);
  ALU alu_1 (.I_Type_In(I_Type), .A_Sel_in(A_Value), .B_Sel_in(B_Value), .Imm_in(Imm), .OpCode(in_1), .out_6(Data));
  registers registers_1 (
    .A_Sel_In(in_2), .B_Sel_In(B_Sel), .C_Sel_In(in_4), .Data_In(Data), .Reg_Write_In(RegWrite),
    .clk_in(Clk), .A_Out(A_Value), .B_Out(B_Value), .Reg0_Out(Reg0_Out), .Reg1_Out(Reg1_Out),
    .Reg2_Out(Reg2_Out), .Reg3_Out(Reg3_Out), .Reg4_Out(Reg4_Out), .Reg5_Out(Reg5_Out), .Reg6_Out(Reg6_Out),
    .Reg7_Out(Reg7_Out), .Reg8_Out(Reg8_Out), .Reg9_Out(Reg9_Out), .Reg10_Out(Reg10_Out),
    .Reg11_Out(Reg11_Out), .Reg12_Out(Reg12_Out), .Reg13_Out(Reg13_Out), .Reg14_Out(Reg14_Out),
    .Reg15_Out(Reg15_Out));
  Counter PC (.Q(PC_out), .clk(Clk));  // open: load, D, count, carry, clr

  assign Instruction_Address_Out = {in_1, Clk};

  // Other names for the same wires on the sheet: A_Sel[3:0] = in_2; C_Sel[3:0] = in_4; ClkIn = Clk;
  //   Instruction_Address[4:0] = {in_1, Clk}; OpCode[3:0] = in_1; Reg0[3:0] = Reg0_Out; Reg1[3:0] = Reg1_Out;
  //   Reg2[3:0] = Reg2_Out; Reg3[3:0] = Reg3_Out; Reg4[3:0] = Reg4_Out; Reg5[3:0] = Reg5_Out; Reg6[3:0] = Reg6_Out;
  //   Reg7[3:0] = Reg7_Out; Reg8[3:0] = Reg8_Out; Reg9[3:0] = Reg9_Out; Reg10[3:0] = Reg10_Out;
  //   Reg11[3:0] = Reg11_Out; Reg12[3:0] = Reg12_Out; Reg13[3:0] = Reg13_Out; Reg14[3:0] = Reg14_Out;
  //   Reg15[3:0] = Reg15_Out
endmodule

// Registers
module registers (
  input  [3:0] A_Sel_In,
  input  [3:0] B_Sel_In,
  input  [3:0] C_Sel_In,
  input  [3:0] Data_In,
  input  Reg_Write_In,
  input  clk_in,
  output [3:0] A_Out,
  output [3:0] B_Out,
  output [3:0] Reg0_Out,
  output [3:0] Reg1_Out,
  output [3:0] Reg2_Out,
  output [3:0] Reg3_Out,
  output [3:0] Reg4_Out,
  output [3:0] Reg5_Out,
  output [3:0] Reg6_Out,
  output [3:0] Reg7_Out,
  output [3:0] Reg8_Out,
  output [3:0] Reg9_Out,
  output [3:0] Reg10_Out,
  output [3:0] Reg11_Out,
  output [3:0] Reg12_Out,
  output [3:0] Reg13_Out,
  output [3:0] Reg14_Out,
  output [3:0] Reg15_Out
);

  wire Reg_Write0, Reg_Write1, Reg_Write2, Reg_Write3, Reg_Write4, Reg_Write5, Reg_Write6, Reg_Write7,
       Reg_Write8, Reg_Write9, Reg_Write10, Reg_Write11, Reg_Write12, Reg_Write13, Reg_Write14, Reg_Write15;

  Demultiplexer #(.select(4), .enable("false")) demultiplexer_1 (
    .out0(Reg_Write0), .out1(Reg_Write1), .out2(Reg_Write2), .out3(Reg_Write3), .out4(Reg_Write4),
    .out5(Reg_Write5), .out6(Reg_Write6), .out7(Reg_Write7), .out8(Reg_Write8), .out9(Reg_Write9),
    .out10(Reg_Write10), .out11(Reg_Write11), .out12(Reg_Write12), .out13(Reg_Write13), .out14(Reg_Write14),
    .out15(Reg_Write15), .in(Reg_Write_In), .sel(C_Sel_In));
  Multiplexer #(.select(4), .width(4), .enable("false")) multiplexer_1 (
    .in0(Reg0_Out), .in1(Reg1_Out), .in2(Reg2_Out), .in3(Reg3_Out), .in4(Reg4_Out), .in5(Reg5_Out),
    .in6(Reg6_Out), .in7(Reg7_Out), .in8(Reg8_Out), .in9(Reg9_Out), .in10(Reg10_Out), .in11(Reg11_Out),
    .in12(Reg12_Out), .in13(Reg13_Out), .in14(Reg14_Out), .in15(Reg15_Out), .out(A_Out), .sel(A_Sel_In));
  Register #(.width(4)) register_1 (.D(Data_In), .en(Reg_Write0), .Q(Reg0_Out), .clk(clk_in));  // open: clr
  Register #(.width(4)) register_2 (.D(Data_In), .en(Reg_Write1), .Q(Reg1_Out), .clk(clk_in));  // open: clr
  Register #(.width(4)) register_3 (.D(Data_In), .en(Reg_Write2), .Q(Reg2_Out), .clk(clk_in));  // open: clr
  Register #(.width(4)) register_4 (.D(Data_In), .en(Reg_Write3), .Q(Reg3_Out), .clk(clk_in));  // open: clr
  Register #(.width(4)) register_5 (.D(Data_In), .en(Reg_Write4), .Q(Reg4_Out), .clk(clk_in));  // open: clr
  Register #(.width(4)) register_6 (.D(Data_In), .en(Reg_Write5), .Q(Reg5_Out), .clk(clk_in));  // open: clr
  Register #(.width(4)) register_7 (.D(Data_In), .en(Reg_Write6), .Q(Reg6_Out), .clk(clk_in));  // open: clr
  Register #(.width(4)) register_8 (.D(Data_In), .en(Reg_Write7), .Q(Reg7_Out), .clk(clk_in));  // open: clr
  Multiplexer #(.select(4), .width(4), .enable("false")) multiplexer_2 (
    .in0(Reg0_Out), .in1(Reg1_Out), .in2(Reg2_Out), .in3(Reg3_Out), .in4(Reg4_Out), .in5(Reg5_Out),
    .in6(Reg6_Out), .in7(Reg7_Out), .in8(Reg8_Out), .in9(Reg9_Out), .in10(Reg10_Out), .in11(Reg11_Out),
    .in12(Reg12_Out), .in13(Reg13_Out), .in14(Reg14_Out), .in15(Reg15_Out), .out(B_Out), .sel(B_Sel_In));
  Register #(.width(4)) register_9 (.D(Data_In), .en(Reg_Write8), .Q(Reg8_Out), .clk(clk_in));  // open: clr
  Register #(.width(4)) register_10 (.D(Data_In), .en(Reg_Write9), .Q(Reg9_Out), .clk(clk_in));  // open: clr
  Register #(.width(4)) register_11 (.D(Data_In), .en(Reg_Write10), .Q(Reg10_Out), .clk(clk_in));  // open: clr
  Register #(.width(4)) register_12 (.D(Data_In), .en(Reg_Write11), .Q(Reg11_Out), .clk(clk_in));  // open: clr
  Register #(.width(4)) register_13 (.D(Data_In), .en(Reg_Write12), .Q(Reg12_Out), .clk(clk_in));  // open: clr
  Register #(.width(4)) register_14 (.D(Data_In), .en(Reg_Write13), .Q(Reg13_Out), .clk(clk_in));  // open: clr
  Register #(.width(4)) register_15 (.D(Data_In), .en(Reg_Write14), .Q(Reg14_Out), .clk(clk_in));  // open: clr
  Register #(.width(4)) register_16 (.D(Data_In), .en(Reg_Write15), .Q(Reg15_Out), .clk(clk_in));  // open: clr

  // Other names for the same wires on the sheet: A[3:0] = A_Out; A_Sel[3:0] = A_Sel_In; B[3:0] = B_Out;
  //   B_Sel[3:0] = B_Sel_In; C_Sel[3:0] = C_Sel_In; clk = clk_in; Data[3:0] = Data_In; Reg0[3:0] = Reg0_Out;
  //   Reg1[3:0] = Reg1_Out; Reg2[3:0] = Reg2_Out; Reg3[3:0] = Reg3_Out; Reg4[3:0] = Reg4_Out; Reg5[3:0] = Reg5_Out;
  //   Reg6[3:0] = Reg6_Out; Reg7[3:0] = Reg7_Out; Reg8[3:0] = Reg8_Out; Reg9[3:0] = Reg9_Out; Reg10[3:0] = Reg10_Out;
  //   Reg11[3:0] = Reg11_Out; Reg12[3:0] = Reg12_Out; Reg13[3:0] = Reg13_Out; Reg14[3:0] = Reg14_Out;
  //   Reg15[3:0] = Reg15_Out; Reg_Write = Reg_Write_In
endmodule

module ALU (
  input  I_Type_In,
  input  [3:0] A_Sel_in,
  input  [3:0] B_Sel_in,
  input  [3:0] Imm_in,
  input  [3:0] OpCode,
  output [3:0] out_6
);

  wire [3:0] ADD, AND, multiplexer_1_out, multiplexer_2_out, multiplexer_3_out, multiplexer_4_out,
       multiplexer_5_out, NEG, NOT, OR, SUB, XOR;

  Multiplexer #(.width(4), .enable("false")) multiplexer_1 (
    .in0(B_Sel_in), .in1(Imm_in), .out(multiplexer_1_out), .sel(I_Type_In));
  Multiplexer #(.width(4), .enable("false")) multiplexer_2 (
    .in0(B_Sel_in), .in1(Imm_in), .out(multiplexer_2_out), .sel(I_Type_In));
  Multiplexer #(.width(4), .enable("false")) multiplexer_3 (
    .in0(B_Sel_in), .in1(Imm_in), .out(multiplexer_3_out), .sel(I_Type_In));
  assign NOT = ~A_Sel_in;  // NOT_Gate not_1, 4 bits wide
  Multiplexer #(.width(4), .enable("false")) multiplexer_4 (
    .in0(B_Sel_in), .in1(Imm_in), .out(multiplexer_4_out), .sel(I_Type_In));
  Multiplexer #(.width(4), .enable("false")) multiplexer_5 (
    .in0(B_Sel_in), .in1(Imm_in), .out(multiplexer_5_out), .sel(I_Type_In));
  assign AND = A_Sel_in & multiplexer_1_out;  // AND_Gate and_1, 4 bits wide
  assign OR = A_Sel_in | multiplexer_2_out;  // OR_Gate or_1, 4 bits wide
  assign XOR = A_Sel_in ^ multiplexer_3_out;  // XOR_Gate xor_1, 4 bits wide
  Negator #(.width(4)) negator_1 (.in(A_Sel_in), .out(NEG));
  Adder #(.width(4)) adder_1 (.a(A_Sel_in), .b(multiplexer_4_out), .out(ADD));  // open: cin, cout
  Subtractor #(.width(4)) subtractor_1 (.a(A_Sel_in), .b(multiplexer_5_out), .out(SUB));  // open: bin, bout
  Multiplexer #(.select(4), .width(4), .enable("false")) multiplexer_6 (
    .in2(A_Sel_in), .in3(Imm_in), .in4(AND), .in5(AND), .in6(OR), .in7(OR), .in8(XOR), .in9(XOR), .in10(NEG),
    .in11(NOT), .in12(ADD), .in13(ADD), .in14(SUB), .in15(SUB), .out(out_6), .sel(OpCode));  // open: in0, in1

  // Other names for the same wires on the sheet: B_Sel[3:0] = B_Sel_in; C_out[3:0] = out_6; I_Type = I_Type_In;
  //   Imm[3:0] = Imm_in; LOAD[3:0] = Imm_in; A_Sel[3:0] = A_Sel_in; MOV[3:0] = A_Sel_in; OP[3:0] = OpCode
endmodule
